// Logisim project FINAL PROJECT.circ as structural Verilog: 5 circuits, main circuit main
module main (
  input  A3,
  input  A2,
  input  A1,
  input  A0,
  input  B3,
  input  B2,
  input  B1,
  input  B0,
  input  in_9,
  output A___B_____A_IS_GREATER_THAN_B,
  output A___B___A_EGQUALS_B,
  output A___B_____B_IS_LESSER_THAN_B
);

  comparator COMPARATOR (
    .CONTROL(in_9), .A3(A3), .A2(A2), .A1(A1), .A0(A0), .B3(B3), .B2(B2), .B1(B1), .B0(B0),
    .A___B(A___B_____A_IS_GREATER_THAN_B), .A___B_2(A___B___A_EGQUALS_B),
    .A___B_3(A___B_____B_IS_LESSER_THAN_B));
endmodule

module comparator (
  input  A3,
  input  A2,
  input  A1,
  input  A0,
  input  B3,
  input  B2,
  input  B1,
  input  B0,
  input  CONTROL,
  output A___B,
  output A___B_2,
  output A___B_3
);

  wire and_1_out, and_2_out, and_3_out, and_4_out, and_5_out, and_6_out, and_7_out, and_8_out, and_9_out,
       and_10_out, and_11_out, and_12_out, and_13_out, and_14_out, n2_s_compliment_invertor_1_out_6,
       n2_s_compliment_invertor_1_out_7, n2_s_compliment_invertor_1_out_8, n2_s_compliment_invertor_1_out_9,
       n2_s_compliment_invertor_2_out_6, n2_s_compliment_invertor_2_out_7, n2_s_compliment_invertor_2_out_8,
       n2_s_compliment_invertor_2_out_9, nor_1_out, nor_2_out, nor_3_out, nor_4_out, not_1_out, not_2_out,
       not_3_out, not_4_out, not_5_out, not_6_out, not_7_out, not_8_out;

  not not_1 (not_1_out, n2_s_compliment_invertor_1_out_6);
  _2_s_Compliment_invertor u_2_s_compliment_invertor_1 (
    .CONTROL(CONTROL), ._3(A3), ._2(A2), ._1(A1), ._0(A0), .out_6(n2_s_compliment_invertor_1_out_6),
    .out_7(n2_s_compliment_invertor_1_out_7), .out_8(n2_s_compliment_invertor_1_out_8),
    .out_9(n2_s_compliment_invertor_1_out_9));  // open: out_10
  not not_2 (not_2_out, n2_s_compliment_invertor_1_out_7);
  not not_3 (not_3_out, n2_s_compliment_invertor_1_out_8);
  not not_4 (not_4_out, n2_s_compliment_invertor_1_out_9);
  _2_s_Compliment_invertor u_2_s_compliment_invertor_2 (
    .CONTROL(CONTROL), ._3(B3), ._2(B2), ._1(B1), ._0(B0), .out_6(n2_s_compliment_invertor_2_out_6),
    .out_7(n2_s_compliment_invertor_2_out_7), .out_8(n2_s_compliment_invertor_2_out_8),
    .out_9(n2_s_compliment_invertor_2_out_9));  // open: out_10
  not not_5 (not_5_out, n2_s_compliment_invertor_2_out_6);
  not not_6 (not_6_out, n2_s_compliment_invertor_2_out_7);
  not not_7 (not_7_out, n2_s_compliment_invertor_2_out_8);
  not not_8 (not_8_out, n2_s_compliment_invertor_2_out_9);
  and and_1 (and_1_out, not_1_out, n2_s_compliment_invertor_2_out_6);
  and and_2 (and_2_out, n2_s_compliment_invertor_1_out_6, not_5_out);
  and and_3 (and_3_out, not_2_out, n2_s_compliment_invertor_2_out_7);
  and and_4 (and_4_out, n2_s_compliment_invertor_1_out_7, not_6_out);
  and and_5 (and_5_out, not_3_out, n2_s_compliment_invertor_2_out_8);
  and and_6 (and_6_out, n2_s_compliment_invertor_1_out_8, not_7_out);
  and and_7 (and_7_out, not_4_out, n2_s_compliment_invertor_2_out_9);
  and and_8 (and_8_out, n2_s_compliment_invertor_1_out_9, not_8_out);
  nor nor_1 (nor_1_out, and_1_out, and_2_out);
  nor nor_2 (nor_2_out, and_3_out, and_4_out);
  nor nor_3 (nor_3_out, and_5_out, and_6_out);
  nor nor_4 (nor_4_out, and_7_out, and_8_out);
  and and_9 (and_9_out, nor_1_out, and_3_out);
  and and_10 (and_10_out, nor_1_out, and_4_out);
  and and_11 (and_11_out, nor_1_out, nor_2_out, and_5_out);
  and and_12 (and_12_out, nor_1_out, nor_2_out, and_6_out);
  and and_13 (and_13_out, nor_1_out, nor_2_out, nor_3_out, and_7_out);
  and and_14 (and_14_out, nor_1_out, nor_2_out, nor_3_out, and_8_out);
  or or_1 (A___B, and_2_out, and_10_out, and_12_out, and_14_out);
  and and_15 (A___B_2, nor_1_out, nor_2_out, nor_3_out, nor_4_out);
  or or_2 (A___B_3, and_1_out, and_9_out, and_11_out, and_13_out);
endmodule

module HALF_ADDER (
  input  A,
  input  A_2,
  output SUM,
  output CARRY
);

  xor xor_1 (SUM, A, A_2);
  and and_1 (CARRY, A, A_2);
endmodule

module _2_s_Compliment_invertor (
  input  _3,
  input  _2,
  input  _1,
  input  _0,
  input  CONTROL,
  output out_6,
  output out_7,
  output out_8,
  output out_9,
  output out_10
);

  wire half_adder_2_carry, half_adder_3_carry, half_adder_4_carry, xor_1_out, xor_2_out, xor_3_out, xor_4_out;

  xor xor_1 (xor_1_out, CONTROL, _3);
  HALF_ADDER half_adder_1 (.A(half_adder_2_carry), .A_2(xor_1_out), .SUM(out_6), .CARRY(out_10));
  xor xor_2 (xor_2_out, CONTROL, _2);
  HALF_ADDER half_adder_2 (.A(half_adder_3_carry), .A_2(xor_2_out), .SUM(out_7), .CARRY(half_adder_2_carry));
  xor xor_3 (xor_3_out, CONTROL, _1);
  HALF_ADDER half_adder_3 (.A(half_adder_4_carry), .A_2(xor_3_out), .SUM(out_8), .CARRY(half_adder_3_carry));
  xor xor_4 (xor_4_out, CONTROL, _0);
  HALF_ADDER half_adder_4 (.A(CONTROL), .A_2(xor_4_out), .SUM(out_9), .CARRY(half_adder_4_carry));
endmodule

module CONTROL (
  input  CONTROL
);
endmodule
